# Fritzing sketch Untitled Sketch 2 (saved by Fritzing 0.9.6b)
circuit board: 8.46667cm x 5.64444cm

parts:
  VCC1 = Battery block 9V
  C1 = Ceramic Capacitor [capacitance=10µF voltage=50V package="0603 [SMD, multilayer]"]
  Q2 = PNP-Transistor [package="TO92 [THT]"]
  U2 = RELAY [package=OJ]
  C2 = Ceramic Capacitor [capacitance=100µF voltage=50V package="0603 [SMD, multilayer]"]
  LED1 = smd LED [color="Red (633nm)" package="0805 [SMD]"]
  LED2 = LED - 5mm [color="Green (560nm)" current=0.030 package="5 mm [THT]"]
  D1 = Rectifier Diode [part_number=1N4007 package="Melf DO-213 AB [SMD]"]
  R2 = Resistor [tolerance=±5% resistance=4.7k package="1206 [SMD]"]
  R1 = Resistor [tolerance=±5% resistance=1k package="1206 [SMD]"]

nets:
  N1: VCC1.-, U2.NO
  N2: VCC1.+, C1.1, Q2.E
  N3: C1.0, R2.Pin_0, R1.Pin_0
  N4: Q2.B, R1.Pin_1
  N5: Q2.C, D1.cathode
  N6: U2.COIL2, C2.0, LED1.anode, LED2.anode, D1.anode
  N7: U2.MAIN, LED1.cathode, LED2.cathode, R2.Pin_1
  N8: U2.COIL1, C2.1
